# Fritzing sketch Connected_Hive_receiving_fritzing (saved by Fritzing 0.9.3b)
breadboards: 1

parts:
  J1 = STM32 Nucleo boards
  A1 = Seeed wio-e5
  Composant1 = LCD1602-I2C

nets:
  N1: J1.D8, A1.Pin_4
  N2: J1.A4/SDA, Composant1.SDA
  N3: J1.A5/SCL, Composant1.SCL
  N4: J1.D2, A1.Pin_3
  5V: J1.5V, A1.Pin_2, Composant1.VCC
  GND: J1.GND, A1.Pin_1, Composant1.GND

notes:
  LoRa E5
  Jaune Rx-micro(PA10(D2)).Tx-LoRa
  Blanc Tx-micro(PA9(D8)).Rx-Lora
  LCD(Tableau de bord)
  Blanc SDA
  Jaune SCL

custom parts:
  Seeed wio-e5: text
  LCD1602-I2C: A standard character display, usually with 2x16 characters. Comes in many colors with LCM1602 IIC attached.
