# Fritzing sketch Connected_Hive_sending_fritzing (saved by Fritzing 0.9.3b)
breadboards: 1

parts:
  DHT1 = Humidity and Temperature Sensor DHT11
  J1 = STM32 Nucleo boards
  Composant1 = LCD1602-I2C
  Composant2 = Adafruit SHT31-D [part_number="Adafruit #2857"]
  Composant3 = HX711 Weighing Sensor Module
  PIR1 = PIR sensor
  A1 = Seeed wio-e5

nets:
  VCC: DHT1.Vcc, J1.5V, Composant1.VCC, Composant2.VCC, Composant3.VCC, PIR1.VDD, A1.Pin_2
  N1: DHT1.Data-signal, J1.D4
  GND: DHT1.GND_2, J1.GND, Composant1.GND, Composant2.GND, Composant3.GND, PIR1.GND, A1.Pin_1
  N2: J1.A4/SDA#114, Composant3.CK/TX
  N3: J1.A5/SCL#115, Composant3.DO/RX
  N4: J1.D8, A1.Pin_3
  N5: J1.A4/SDA#1159, Composant1.SDA, Composant2.SDA
  N6: J1.A5/SCL#1160, Composant2.SCL
  N7: J1.D2, A1.Pin_4
  N8: J1.D5_PWM, PIR1.SIG

notes:
  DHT11
  Jaune SIG-PB5(D4)
  Blanc NC
  HX711
  Jaune SCK(PC1(A4))
  Blanc DT(PC0(A5))
  PIR
  Jaune SIG-PB4(D5)
  SHT31
  Blanc SDA
  Jaune SCL
  LORA E5
  Jaune Rx-micro(PA10(D2)).Tx-Lora
  Blanc Tx-micro(PA9 (D8)).Rx-Lora
  LCD
  Blanc SDA
  Jaune SCL
  Non Connectée

custom parts:
  Humidity and Temperature Sensor DHT11: Digital relative humidity & temperature sensor DHT11
  LCD1602-I2C: A standard character display, usually with 2x16 characters. Comes in many colors with LCM1602 IIC attached.
  Adafruit SHT31-D: Sensirion Temperature/Humidity sensors are some of the finest & highest-accuracy devices you can get. And, finally we have some that have a true I2C interface for easy reading. The SHT31-D sensor has an excellent ±2% relative humidity and ±0.3°C accuracy for most uses. We now use the version with a PTFE filter, it'll stay clean while still allowing humidity measurements to work Unlike earlier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
  Seeed wio-e5: text
